# Fritzing sketch Untitled Sketch (saved by Fritzing 0.8.7b)
breadboards: 1

parts:
  R = Resistor [tolerance=±5% resistance=220 package=THT]
  V = Battery
  C = Ceramic Capacitor [capacitance=100nF package="100 mil [THT, multilayer]"]

nets:
  N1: R.Pin_0, V.+
  N2: R.Pin_1, C.1
  N3: V.-, C.0
